# Fritzing sketch proyecto Instrumentacion virtual (saved by Fritzing 0.9.8b)
breadboards: 1

parts:
  HC-SR04_Sensor_1 = HC-SR04 Ultrasonic Distance Sensor
  JACK1 = 2.1mm Barrel Jack with Terminal Block
  VALVE1 = Plastic Solenoid Valve
  Componente1 = Arduino Uno (Rev3)
  S1 = H-Bridge with L298N
  12V_DC_Pump1 = DC Motor
  DS2 = DS18B20 1-Wire Temperature Sensor [part_number=DS18B20]
  YF-S201_Flow_Meter2 = YF-S201 Water Flow Meter
  KY-1 = Keyes Relay [package=THT]
  LED1 = LED - 5mm [color="Red (633nm)" current=0.030 package="5 mm [THT]"]
  R1 = Resistor [tolerance=±5% power=0.25 resistance=220 package=THT]

nets:
  VCC: HC-SR04_Sensor_1.VCC, Componente1.5V, DS2.VDD, YF-S201_Flow_Meter2.VCC, KY-1.power
  N1: HC-SR04_Sensor_1.TRIG, Componente1.D10_PWM/SS
  N2: HC-SR04_Sensor_1.ECHO, Componente1.D9_PWM
  GND: HC-SR04_Sensor_1.GND, JACK1.NEG, Componente1.GND, S1.GND, DS2.GND, YF-S201_Flow_Meter2.GND, KY-1.ground, KY-1.C, R1.Pin_0
  N3: JACK1.POS, VALVE1.no_name_yet#1, S1.12V
  N4: VALVE1.no_name_yet#2, KY-1.NO
  N5: Componente1.D8, KY-1.signal
  N6: Componente1.D11_PWM/MOSI, S1.ENA
  N7: Componente1.D12/MISO, S1.IN1
  N8: Componente1.D13/SCK, S1.IN2
  N9: Componente1.D2, YF-S201_Flow_Meter2.SIG
  N10: Componente1.D3_PWM, DS2.DQ
  N11: S1.M1-01, 12V_DC_Pump1.pin_2
  N12: S1.M1-02, 12V_DC_Pump1.pin_1
  N13: LED1.cathode, R1.Pin_1

notes:
  BOMBA DE AGUA 12V
  Sensor de Temperatura
  Protegido contra Agua
  DS18B20
  Medición de Nivel
  Ultrasonico
  Adaptador de entrada de la fuente de Voltaje 12v
  Nota la electrovalvula es opcional en el proyecto
  Nota: en caso de no usar electrovalvula conecte un LED en el puerto 8 para simular su activación
  Materia: Fundamentos de Instrumentación Virtual
  Profesor: M.C. Rubén Loredo Amaro
  Mi Github:
  https://github.com/ruben-loredo/Instrumentacion-Virtual-Arduino
  Canal de youtube
  https://www.youtube.com/user/rubyck71
  Sensor de Flujo de Agua
  YF-S201

custom parts:
  H-Bridge with L298N: h-bridge
  YF-S201 Water Flow Meter: The YF-S201 Flow Meter. The input voltage is 5V to 24V (DC).
  Keyes Relay: The Keyes 5V relay module is suitable for SCM development, home appliance control. It uses a 5V~12V TIL control signal which can control DC / AC signal.

// code stored in the sketch: Proyecto_Instrumentacion_Tanque_v1.ino
/* Control de "Nivel de agua en un tanque"
    Profesor: Rubén Loredo Amaro 
    Materia: Fundamentos de Instrumentación Virtual
    Agosto del 2021 V1
    https://github.com/ruben-loredo/Instrumentacion-Virtual-Arduino
*/
#include <OneWire.h>
#include <DallasTemperature.h>
//------------puente H L298N----------------
const int ENA = 11;
const int IN1 = 12;
const int IN2 = 13;
//--------------ultrasonico -----------------
const int PinTrig = 10;
const int PinEcho = 9;
const float VelSon = 34000.0;
float distancia;
//--------------Caudalimetro-----------------
unsigned char flowsensor = 2;
//--------------Electrovalvula---------------
const int valvula = 8;
//-------------------------------------------
String StatusValvula = "";
int duty;
int datoSerie;
String inString = "";         // string to hold input
volatile int flow_frequency;  // Measures flow sensor pulses
unsigned int l_hour;          // Calculated litres/hour
unsigned long currentTime;
unsigned long cloopTime;

OneWire ourWire(3);                //Se establece el pin 2  como bus OneWire
DallasTemperature sensors(&ourWire); //Se declara una variable u objeto para nuestro sensor
/*Función que hace el conteo del flujo de los pulsos del sensor
   de agua esta función es un interrupción del programa principal
*/
void flow () // Interrupt function
{
  flow_frequency++;
}

//-----------------------------------------------------------------------
/*Funcion que controla el puente H L298N de
  la bomba de agua
*/
void bomba(int vel)
{
  //------ CW ----------
  digitalWrite(IN1, HIGH);
  digitalWrite(IN2, LOW);
  //---------------------
  analogWrite(ENA, vel);
}

/*Función que lee datos numericos enteros por el puerto serie
   y los retorna en la función
*/
int readNum() {
  int intNum = 0;
  while (true)
  {
    if (Serial.available() > 0) {
      int inChar = Serial.read();
      if (isDigit(inChar)) {

        inString += (char)inChar;
      }
      if (inChar == '\n') {
        intNum = inString.toInt();
        inString = "";
        return (intNum);
        break;
      }
    }
  }
}
//-----------------------------------------------------------------------
void WaterFlowSensorYF_S201() {
  currentTime = millis();
  // Every second, calculate and print litres/hour
  if (currentTime >= (cloopTime + 1000))
  {
    cloopTime = currentTime; // Updates cloopTime
    // Pulse frequency (Hz) = 7.5Q, Q is flow rate in L/min.
    l_hour = (flow_frequency * 60 / 7.5); // (Pulse frequency x 60 min) / 7.5Q = flowrate in L/hour
    flow_frequency = 0; // Reset Counter
    Serial.print("F=");
    Serial.println(l_hour, DEC); // Print litres/hour
  }
}
//-----------------------------------------------------------------------
void SensorUltrasonico()
{
  // Ponemos el Triiger en estado bajo y esperamos 2 ms
  digitalWrite(PinTrig, LOW);
  delayMicroseconds(2);

  // Ponemos el pin Trigger a estado alto y esperamos 10 ms
  digitalWrite(PinTrig, HIGH);
  delayMicroseconds(10);

  // Comenzamos poniendo el pin Trigger en estado bajo
  digitalWrite(PinTrig, LOW);


  unsigned long tiempo = pulseIn(PinEcho, HIGH);  // La función pulseIn obtiene el tiempo entre estados, en este caso a HIGH
  distancia = tiempo * 0.000001 * VelSon / 2.0;   // Obtenemos la distancia en cm
  Serial.print("D=");
  Serial.println(distancia);

}

void SensorTempDS1820() {
  sensors.requestTemperatures();   //Se envía el comando para leer la temperatura
  float temp = sensors.getTempCByIndex(0); //Se obtiene la temperatura en ºC

  Serial.print("T=");
  Serial.println(temp);
}

//-----------------------------------------------------------------------
void setup() {
  // Ponemos el pin Trig en modo salida
  pinMode(PinTrig, OUTPUT);
  // Ponemos el pin Echo en modo entrada
  pinMode(PinEcho, INPUT);
  //--------- CONFIGURA PUENTE H ----------
  pinMode(ENA, OUTPUT);
  pinMode(IN1, OUTPUT);
  pinMode(IN2, OUTPUT);
  //--------- CONFIGURA CAUDALIMETRO----------
  pinMode(flowsensor, INPUT);
  //--------- CONFIGURA ELECTROVALVULA----------
  pinMode(valvula, OUTPUT);
  digitalWrite(valvula, LOW);   //inicializa en estado bajo
  StatusValvula = "0";
  //-------inicializa Sensor Temperatura----------------
  sensors.begin();
  //---------------------------------------------------
  digitalWrite(flowsensor, HIGH); // Optional Internal Pull-Up
  attachInterrupt(0, flow, RISING); // Setup Interrupt
  sei(); // Enable interrupts
  currentTime = millis();
  cloopTime = currentTime;

  // configura el puerto Serie
  Serial.begin(9600);

  while (!Serial) {
    ; // Espera a conectarse.
  }
}

void loop() {
  
  if (Serial.available() > 0)
  {
    datoSerie = Serial.read();
    switch (datoSerie) {
      case 'A':
        digitalWrite(valvula, HIGH);
        StatusValvula = "1";
        break;
      case 'a':
        digitalWrite(valvula, LOW);
        StatusValvula = "0";
        break;
      case 'b' :
        duty = readNum();
        bomba(duty);
        Serial.print("b");
        Serial.println(duty);
        break;

    }
  }
  Serial.print("B=");
  Serial.println(duty);

  Serial.print("V=");
  Serial.println(StatusValvula);

  WaterFlowSensorYF_S201();   //funcion que envia datos del sensor de flujo

  SensorUltrasonico();        //funcion que envia datos del sensor ultrasonico

  SensorTempDS1820();         //funcion que envia datos del sensor de temperatura


  delay(500);

}
